# Fritzing sketch project1 (saved by Fritzing 0.9.3b)
breadboards: 1

parts:
  R1 = Resistor [tolerance=±5% resistance=220 package=THT]
  Part1 = Arduino Uno (Rev3)
  LED1 = smd LED [color="Red (633nm)" package="0805 [SMD]"]
  LED2 = smd LED [color="Red (633nm)" package="0805 [SMD]"]
  LED3 = smd LED [color="Red (633nm)" package="0805 [SMD]"]
  Part3 = Bluetooth HC-05 Macho
  R2 = Resistor [tolerance=±5% resistance=220 package=THT]
  R3 = Resistor [tolerance=±5% resistance=220 package=THT]
  R4 = Resistor [tolerance=±5% resistance=220 package=THT]
  R5 = Resistor [tolerance=±5% resistance=220 package=THT]

nets:
  N1: R1.Pin_0, Part1.D5_PWM
  N2: R1.Pin_1, LED2.anode
  GND: Part1.GND, LED1.cathode, LED2.cathode, LED3.cathode, Part3.GND, R5.Pin_1
  N3: Part1.D0/RX, Part3.TXD
  N4: Part1.D1/TX, R4.Pin_0
  N5: Part1.D3_PWM, R3.Pin_0
  N6: Part1.D4, R2.Pin_0
  5V: Part1.5V, Part3.VCC
  N7: LED1.anode, R3.Pin_1
  N8: LED3.anode, R2.Pin_1
  N9: Part3.RXD, R4.Pin_1, R5.Pin_0

// code stored in the sketch: Untitled2.ino
int led1 = 4;
int led2 = 6;
int led3 = 8;


void setup() {
  pinMode(led1, OUTPUT);
  pinMode(led2, OUTPUT);
  pinMode(led3, OUTPUT);
  Serial.begin(9600);
}


void loop() {
  if (Serial.available()) {
    String command = Serial.readStringUntil('\n'); 


    command.trim(); 


    if (command.equalsIgnoreCase("ON1")) {
      digitalWrite(led1, HIGH);
      digitalWrite(led2, LOW);
      digitalWrite(led3, LOW);
    }
    else if (command.equalsIgnoreCase("ON2")) {
      digitalWrite(led2, HIGH);
      digitalWrite(led1, LOW);
      digitalWrite(led3, LOW);
    }
    else if (command.equalsIgnoreCase("ON3")) {
      digitalWrite(led3, HIGH);
      digitalWrite(led1, LOW);
      digitalWrite(led2, LOW);
    }
    else if (command.equalsIgnoreCase("ONALL")) {
      digitalWrite(led1, HIGH);
      digitalWrite(led2, HIGH);
      digitalWrite(led3, HIGH);
    }
    else {
      digitalWrite(led1, LOW);
      digitalWrite(led2, LOW);
      digitalWrite(led3, LOW);
    }
  }
}
